# Fritzing sketch SorticRoboter_with_CommunicationHub_electrical_shematic (saved by Fritzing 0.9.3b)

parts:
  Bauteil3 = Adafruit 4-channel I2C-safe Bi-directional Logic Level Converter [part_number="Adafruit #757"]
  ESP32_DevKit_ESP32-WROOM1 = ESP32 DevKit ESP32-WROOM [part_number="ESP32 DevKit ESP32-WROOM"]
  Arduino_UNO = Arduino Uno (Rev3)
  RFID_Reader = RFID-RC522-v2

nets:
  GND: Bauteil3.GND, ESP32_DevKit_ESP32-WROOM1.GND, Arduino_UNO.GND, RFID_Reader.GND
  N1: Bauteil3.A2, ESP32_DevKit_ESP32-WROOM1.GPIO21
  N2: Bauteil3.A1, ESP32_DevKit_ESP32-WROOM1.GPIO22
  N3: Bauteil3.LV, ESP32_DevKit_ESP32-WROOM1.3.3V
  N4: Bauteil3.B2, Arduino_UNO.A4/SDA
  N5: Bauteil3.B1, Arduino_UNO.A5/SCL
  N6: Bauteil3.HV, Arduino_UNO.5V
  N7: Arduino_UNO.D9_PWM, RFID_Reader.RST
  N8: Arduino_UNO.D11_PWM/MOSI, RFID_Reader.MOSI
  N9: Arduino_UNO.D12/MISO, RFID_Reader.MISO
  N10: Arduino_UNO.D13/SCK, RFID_Reader.SCK
  3V3: Arduino_UNO.3V3, RFID_Reader.3.3V

custom parts:
  Adafruit 4-channel I2C-safe Bi-directional Logic Level Converter: Because the Arduino (and Basic Stamp) are 5V devices, and most modern sensors, displays, flash cards and modes are 3.3V-only, many makers find that they need to perform level shifting/conversion to protect the 3.3V device from 5V. We do have some other handy level shifters in the shop, from the DIP 74LVC245 to the fancy bi-directional TXB0108. However, neither of these are happy to work with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
  ESP32 DevKit ESP32-WROOM: ESP32-WROOM-32 is a powerful, generic Wi-Fi+BT+BLE MCU module that targets a wide variety of applications, ranging from low-power sensor networks to the most demanding tasks, such as voice encoding, music streaming and MP3 decoding. At the core of this module is the ESP32-D0WDQ6 chip*. The chip embedded is designed to be scalable and adaptive. There are two CPU cores that can be individually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
  RFID-RC522-v2: A simple China made RFID-RC522 Reader; do check the pin labels, as this is a MFRC522 based clone.
